# Fritzing sketch TTGO_DHT11_bme280 (saved by Fritzing 0.9.10b)
breadboards: 1

parts:
  X1 = LilyGo TTGO LoRa32 T3 V1.6.1
  A1 = GY-BMP280 Breakout
  DHT1 = DHT11 Humitidy and Temperature Sensor (3 pins)  # not connected

nets:
  N1: X1.GND#1, A1.Pin_2
  N2: X1.3V3, A1.Pin_1
  N3: X1.21, A1.Pin_3
  N4: X1.22, A1.Pin_4

notes:
  DHT11 - Pin 14
  BME280 - 21 y 22

custom parts:
  LilyGo TTGO LoRa32 T3 V1.6.1: WSP32 based LoRaWAN Module with OLED
  DHT11 Humitidy and Temperature Sensor (3 pins): DHT11 Humidity and Temperature Sensor (3 pins).
