# Fritzing sketch bme280 (saved by Fritzing 0.9.10b)
breadboards: 1

parts:
  X1 = LilyGo TTGO LoRa32 T3 V1.6.1
  A1 = GY-BMP280 Breakout
  Part1 = DHT22 Breakout module [package="Breakout board"]

nets:
  N1: X1.GND#1, A1.Pin_2, Part1.-
  N2: X1.3V3, A1.Pin_1
  N3: X1.21, A1.Pin_3
  N4: X1.22, A1.Pin_4

notes:
  DHT - Pin 4
  BME280 - 21 y 22

custom parts:
  LilyGo TTGO LoRa32 T3 V1.6.1: WSP32 based LoRaWAN Module with OLED
  DHT22 Breakout module: DHT22 temperature and humidity sensor module, provides a low-latency serial interface to measure humidity and temperature.
